# Fritzing sketch Sketch 2 (saved by Fritzing 1.0.4)
circuit board: 12cm x 7.5cm
breadboards: 1

parts:
  A1 = Arduino Nano ESP32
  S1 = Momentary Switch [package=ksa_sealed_tac_switch]
  A2 = Waveshare e-Paper HAT with 7in display [package=THT]
  J1 = male pin header, 8 pins [form="♂ (male)"]
  R2 = Rotary Potentiometer (Large) [maximum_resistance=20kΩ knob_status=50% power=0.5W package=THT]
  R3 = Resistor [tolerance=±5% power=0.25W resistance=1M package=THT]
  R4 = Resistor [tolerance=±5% power=0.25W resistance=1M package=THT]
  C2 = Electrolytic Capacitor [capacitance=1µF voltage=35V package="100 mil [THT, electrolytic]"]
  S2 = Toggle Switch [package=THT]
  U1 = LIPO-1000mAh [package=lipo-1000]
  ZS-042_RTC1 = ZS-042 RTC Module
  Part1 = Adafruit SDIO microSD Breakout
  C1 = Electrolytic Capacitor [capacitance=1µF voltage=35V package="100 mil [THT, electrolytic]"]

nets:
  N1: A1.Pin_2, J1.pin8
  N2: A1.Pin_5, ZS-042_RTC1.VCC
  N3: A1.Pin_6, ZS-042_RTC1.SDA
  N4: A1.Pin_7, ZS-042_RTC1.SCL
  N5: A1.Pin_8, R2.leg2
  N6: A1.Pin_9, R2.wiper, C1.+
  N7: A1.Pin_11, R3.Pin_1, R4.Pin_0, C2.+
  GND: A1.Pin_14, A1.Pin_19, S1.2, J1.pin7, R2.leg1, R4.Pin_1, C2.-, S2.L1, U1.-, ZS-042_RTC1.GND, Part1.GND, C1.-
  N8: A1.Pin_15, R3.Pin_0, S2.COM
  N9: A1.Pin_18, S1.3
  N10: A1.Pin_21, Part1.CS
  N11: A1.Pin_22, Part1.DI
  N12: A1.Pin_23, Part1.DO
  N13: A1.Pin_24, Part1.SCLK
  N14: A1.Pin_25, A2.pin_6, J1.pin6
  N15: A1.Pin_26, A2.pin_5, J1.pin5
  N16: A1.Pin_27, A2.pin_4, J1.pin4
  N17: A1.Pin_28, A2.pin_3, J1.pin3
  N18: A1.Pin_29, A2.pin_2, J1.pin2
  N19: A1.Pin_30, A2.pin_1, J1.pin1
  N20: S2.L2, U1.+

notes:
  BSY
  VCC
  GND
  VIN
  Alessandro
  Crugnola
  2025
  RTC
  SDA
  SCL
  SD-Card
  CS
  DI
  DO
  CLK
  RST

custom parts:
  Arduino Nano ESP32: Arduino® Nano ESP32 tht.
  Waveshare e-Paper HAT with 7in display: .This is a universal driver board for e-Paper raw panels, can be used to drive various SPI interface e-Paper from Waveshare. This version includes a 7in display panel in breadboard.
