# Fritzing sketch Sketch (saved by Fritzing 1.0.4)
circuit board: 13.6783cm x 5.67736cm
breadboards: 1

parts:
  A1 = Arduino Nano ESP32
  S1 = Pushbutton [package="[THT]"]
  S2 = Toggle Switch [package=THT]
  R1 = Resistor [tolerance=±5% power=0.25W resistance=1M package=THT]
  R2 = Resistor [tolerance=±5% power=0.25W resistance=1M package=THT]
  C1 = Electrolytic Capacitor [capacitance=0.1µF voltage=50V package="1010 [SMD, electrolytic]"]
  R3 = Rotary Potentiometer (Large) [maximum_resistance=10kΩ knob_status=50% power=0.5W package=THT]
  ZS-042_RTC1 = ZS-042 RTC Module
  U1 = LIPO-2000mAh [package=lipo-2000]
  Part1 = Adafruit SDIO microSD Breakout
  A2 = Waveshare e-Paper HAT with 7in display [package=THT]
  C3 = Electrolytic Capacitor [capacitance=0.1µF voltage=50V package="1010 [SMD, electrolytic]"]

nets (from the breadboard view):
  N1: A1.Pin_2, A2.pin_8
  N2: A1.Pin_5, ZS-042_RTC1.VCC
  N3: A1.Pin_6, ZS-042_RTC1.SDA
  N4: A1.Pin_7, ZS-042_RTC1.SCL
  N5: A1.Pin_8, R3.leg2
  N6: A1.Pin_9, R3.wiper, C3.+
  N7: A1.Pin_11, R1.Pin_1, R2.Pin_0, C1.+
  N8: A1.Pin_14, A1.Pin_19, S2.L1, R2.Pin_1, C1.-, U1.-
  N9: A1.Pin_15, S2.COM, R1.Pin_0
  N10: A1.Pin_18, S1.Pin_3, S1.Pin_4
  N11: A1.Pin_21, Part1.CS
  N12: A1.Pin_22, Part1.DI
  N13: A1.Pin_23, Part1.DO
  N14: A1.Pin_24, Part1.SCLK
  N15: A1.Pin_25, A2.pin_6
  N16: A1.Pin_26, A2.pin_5
  N17: A1.Pin_27, A2.pin_4
  N18: A1.Pin_28, A2.pin_3
  N19: A1.Pin_29, A2.pin_2
  N20: A1.Pin_30, A2.pin_1
  GND: S1.Pin_1, S1.Pin_2, R3.leg1, ZS-042_RTC1.GND, Part1.GND, A2.pin_7, C3.-
  N21: S2.L2, U1.+

custom parts:
  Arduino Nano ESP32: Arduino® Nano ESP32 smd.
  Waveshare e-Paper HAT with 7in display: .This is a universal driver board for e-Paper raw panels, can be used to drive various SPI interface e-Paper from Waveshare. This version includes a 7in display panel in breadboard.
