# Fritzing sketch adafruit-huzzah-feather-esp32-v2 (saved by Fritzing 1.0.4)
breadboards: 1

parts:
  Part1 = Adafruit ESP32 Feather V2
  Part2 = Adafruit SDIO microSD Breakout
  S1 = Toggle Switch [package=THT]
  S2 = Pushbutton [package="[SMD]"]
  S3 = Pushbutton [package="[SMD]"]
  R1 = Rotary Potentiometer (Small) [maximum_resistance=100kΩ knob_status=50% power=0.5W package=THT]
  C1 = Electrolytic Capacitor [capacitance=10μF voltage=35V package="0605 [SMD, electrolytic]"]
  R2 = Resistor [tolerance=±5% resistance=10k package="2512 [SMD]"]
  U1 = LIPO-2000mAh [package=lipo-2000]
  A1 = Waveshare e-Paper HAT with 7in display [package=THT]

nets:
  N1: Part1.SDA, Part1.IO27_A10, Part2.CS, A1.pin_2
  N2: Part1.MISO, Part2.DO
  N3: Part1.MOSI, Part2.DI
  N4: Part1.SCK, Part2.SCLK
  N5: Part1.A2_I34, R1.wiper, C1.+
  N6: Part1.A1_DAC1, S2.Pin_3, S2.Pin_4, R2.Pin_1
  GND: Part1.GND, Part2.GND, S3.Pin_1, S3.Pin_2, R1.leg2, C1.-, R2.Pin_0, U1.-, A1.pin_7
  3.3V: Part1.3.3V, Part2.3.3V, S2.Pin_1, S2.Pin_2, A1.pin_8
  N7: Part1.!RESET, S3.Pin_3, S3.Pin_4
  N8: Part1.VBAT, S1.L2
  N9: Part1.IO12_A11, A1.pin_6
  N10: Part1.IO33_A9, A1.pin_3
  N11: Part1.IO15_A8, A1.pin_5
  N12: Part1.IO32_A7, A1.pin_4
  N13: Part1.IO14_A6, A1.pin_1
  N14: Part1.SCL, R1.leg1
  N15: S1.COM, U1.+

custom parts:
  Waveshare e-Paper HAT with 7in display: .This is a universal driver board for e-Paper raw panels, can be used to drive various SPI interface e-Paper from Waveshare. This version includes a 7in display panel in breadboard.
