# Fritzing sketch dfrobot-firebeetle2-esp32-c6 (saved by Fritzing 1.0.4)
breadboards: 1

parts:
  A1 = Firebeetle 2 ESP32-C6
  D1 = SOLAR-IXYS [package=solarbit-12x1]
  Part1 = Adafruit SDIO microSD Breakout
  R2 = Rotary Potentiometer (Small) [maximum_resistance=50kΩ knob_status=50% power=0.5W package=THT]
  R3 = Resistor [tolerance=±5% resistance=10k package="2010 [SMD]"]
  S1 = Toggle Switch [package=THT]
  U1 = LIPO-2000mAh [package=lipo-2000]
  S2 = Pushbutton [package="[SMD]"]
  S3 = Pushbutton [package="[SMD]"]
  C1 = Capacitor Polarized [package=cpol-radial-100uf-25v]
  A2 = Waveshare e-Paper HAT with 7in display [package=THT]

nets:
  N1: A1.Pin_1, S3.Pin_3, S3.Pin_4
  N2: A1.Pin_2, A1.Pin_31, Part1.3.3V, S2.Pin_1, S2.Pin_2, A2.pin_8
  N3: A1.Pin_4, A1.Pin_30, A1.Pin_34, D1.A, Part1.GND, R2.leg1, R3.Pin_0, U1.-, S3.Pin_1, S3.Pin_2, C1.-, A2.pin_7
  N4: A1.Pin_6, Part1.SCLK
  N5: A1.Pin_7, Part1.DI
  N6: A1.Pin_8, Part1.DO
  N7: A1.Pin_9, A2.pin_5
  N8: A1.Pin_10, A2.pin_6
  N9: A1.Pin_11, Part1.CS
  N10: A1.Pin_13, A2.pin_4
  N11: A1.Pin_15, A2.pin_3
  N12: A1.Pin_16, A2.pin_2
  N13: A1.Pin_17, A2.pin_1
  N14: A1.Pin_24, R2.wiper, C1.+
  N15: A1.Pin_27, R3.Pin_1, S2.Pin_3, S2.Pin_4
  N16: A1.Pin_32, D1.C
  N17: A1.Pin_33, S1.L2
  N18: S1.COM, U1.+

custom parts:
  Firebeetle 2 ESP32-C6: FireBeetle 2 ESP32-C6 is a low-power IoT main control board designed based on the ESP32-C6 chip.
  Waveshare e-Paper HAT with 7in display: .This is a universal driver board for e-Paper raw panels, can be used to drive various SPI interface e-Paper from Waveshare. This version includes a 7in display panel in breadboard.
