# Fritzing sketch unexpected maker feather s3 (saved by Fritzing 1.0.4)
breadboards: 1

parts:
  A1 = featherS3
  S1 = Momentary Switch [package=ksa_sealed_tac_switch]
  S2 = Momentary Switch [package=ksa_sealed_tac_switch]
  U1 = SWITCH_SPDT [package=kps-1290]
  R1 = Rotary Potentiometer (Small) [maximum_resistance=50kΩ knob_status=50% power=0.5W package=THT]
  C1 = Electrolytic Capacitor [capacitance=0.1µF voltage=35V package="0807 [SMD, electrolytic]"]
  Part1 = Adafruit SDIO microSD Breakout
  U2 = LIPO-2000mAh [package=lipo-2000]
  A2 = Waveshare e-Paper HAT with 7in display [package=THT]

nets:
  N1: A1.Pin_1, S2.3
  N2: A1.Pin_4, A1.Pin_33, A1.Pin_38, S1.2, S2.2, U1.S, R1.leg2, C1.-, Part1.GND, A2.pin_7
  N3: A1.Pin_5, Part1.DI
  N4: A1.Pin_6, R1.wiper, C1.+
  N5: A1.Pin_7, Part1.SCLK
  N6: A1.Pin_8, Part1.DAT2
  N7: A1.Pin_9, A2.pin_1
  N8: A1.Pin_10, A2.pin_2
  N9: A1.Pin_11, A2.pin_5
  N10: A1.Pin_12, A2.pin_6
  N11: A1.Pin_16, Part1.3.3V, A2.pin_8
  N12: A1.Pin_23, R1.leg1
  N13: A1.Pin_24, A2.pin_4
  N14: A1.Pin_25, S1.3
  N15: A1.Pin_26, Part1.DAT1
  N16: A1.Pin_27, Part1.DO
  N17: A1.Pin_28, A2.pin_3
  N18: A1.Pin_29, A1.Pin_34, Part1.CS
  N19: A1.Pin_30, A1.Pin_36
  N20: A1.Pin_37, U2.-
  N21: U1.P, U2.+

custom parts:
  featherS3: FeatherS3 is the latest in our super popular ESP32 based Feather boards.
  Waveshare e-Paper HAT with 7in display: .This is a universal driver board for e-Paper raw panels, can be used to drive various SPI interface e-Paper from Waveshare. This version includes a 7in display panel in breadboard.
